# Fritzing sketch Diagrama Caracterizacion Motor reductor (saved by Fritzing 0.9.5d)

parts:
  M1 = DOIT Esp32 DevKit v1 (30 pins long, 11 pins width) [part_number=ESP32S-PIN30]
  L298N1 = L298N DC motor driver
  Componente1 = FC-03 [chip_label=FC-03]
  M2 = DC Motor
  BAT1 = Battery Holders [package=battery-aa-panel]  # not connected
  VCC1 = Battery  # not connected
  VCC2 = Battery

nets:
  3V3: M1.3V3, Componente1.VCC
  GND: M1.GND, Componente1.GND, VCC2.-
  N1: M1.D33, Componente1.D0
  N2: M1.D25, L298N1.ENA
  N3: M1.D26, L298N1.IN1
  N4: M1.D27, L298N1.IN2
  N5: L298N1.OUT1, M2.pin_2
  N6: L298N1.OUT2, M2.pin_1

notes:
  Cargador 5V
  Fuente ATX 12V
  Helice
  Driver L298N
  Esp-32
  Encoder FC-03
  Motor TT

custom parts:
  DOIT Esp32 DevKit v1 (30 pins long, 11 pins width): The DOIT Esp32 DevKit v1 is one of the development board created by DOIT to evaluate the ESP-WROOM-32 module. It is based on the ESP32 microcontroller that boasts Wifi, Bluetooth, Ethernet and Low Power support all in a single chip. (vanepp) made breadboard work, adjusted pin numbering and labels and reduced size of schematic and cleaned up pcb. This chip is 30pins long (2 x15) and 11 pins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
  L298N DC motor driver: 2x DC motor driver with 78M05 positive voltage regulator (7..35 V) L298N: max 46 V, 2 A Set 5 V Enable jumper to enable 5 V regultor (needed for the L298N) and +5 V output at screw terminal or supply external +5 V at screw terminal Set ENA and/or ENB to +5 V to enable motor permanently or supply ENA and/or ENB with PWM signal IN1 and IN2 set rotation directory for motor A (OUT1/OUT2) IN2 and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
  FC-03: FC-03, LM393 IR Speed Sensor Encoder
